// Logisim project 2^32 memory with Control.circ as structural Verilog: 3 circuits, main circuit main
module main (
  input  Clk,
  input  [31:0] Address,
  input  MemWrite,
  input  MemRead,
  input  [31:0] Data_In,
  output [31:0] Data_Out
);

  wire decoder_1_out0, decoder_1_out1, decoder_1_out2, decoder_1_out3, decoder_1_out4, decoder_1_out5,
       decoder_1_out6, decoder_1_out7, decoder_2_out0, decoder_2_out1, decoder_2_out2, decoder_2_out3,
       decoder_2_out4, decoder_2_out5, decoder_2_out6, decoder_2_out7, decoder_2_out8, decoder_2_out9,
       decoder_2_out10, decoder_2_out11, decoder_2_out12, decoder_2_out13, decoder_2_out14, decoder_2_out15,
       decoder_2_out16, decoder_2_out17, decoder_2_out18, decoder_2_out19, decoder_2_out20, decoder_2_out21,
       decoder_2_out22, decoder_2_out23, decoder_2_out24, decoder_2_out25, decoder_2_out26, decoder_2_out27,
       decoder_2_out28, decoder_2_out29, decoder_2_out30, decoder_2_out31, decoder_3_out0, decoder_3_out1,
       decoder_3_out2, decoder_3_out3, decoder_3_out4, decoder_3_out5, decoder_3_out6, decoder_3_out7,
       decoder_3_out8, decoder_3_out9, decoder_3_out10, decoder_3_out11, decoder_3_out12, decoder_3_out13,
       decoder_3_out14, decoder_3_out15, decoder_3_out16, decoder_3_out17, decoder_3_out18, decoder_3_out19,
       decoder_3_out20, decoder_3_out21, decoder_3_out22, decoder_3_out23, decoder_3_out24, decoder_3_out25,
       decoder_3_out26, decoder_3_out27, decoder_3_out28, decoder_3_out29, decoder_3_out30, decoder_3_out31,
       decoder_4_out0, decoder_4_out1, decoder_4_out2, decoder_4_out3, decoder_4_out4, decoder_4_out5,
       decoder_4_out6, decoder_4_out7, decoder_4_out8, decoder_4_out9, decoder_4_out10, decoder_4_out11,
       decoder_4_out12, decoder_4_out13, decoder_4_out14, decoder_4_out15, decoder_4_out16, decoder_4_out17,
       decoder_4_out18, decoder_4_out19, decoder_4_out20, decoder_4_out21, decoder_4_out22, decoder_4_out23,
       decoder_4_out24, decoder_4_out25, decoder_4_out26, decoder_4_out27, decoder_4_out28, decoder_4_out29,
       decoder_4_out30, decoder_4_out31, decoder_5_out0, decoder_5_out1, decoder_5_out2, decoder_5_out3,
       decoder_5_out4, decoder_5_out5, decoder_5_out6, decoder_5_out7, decoder_5_out8, decoder_5_out9,
       decoder_5_out10, decoder_5_out11, decoder_5_out12, decoder_5_out13, decoder_5_out14, decoder_5_out15,
       decoder_5_out16, decoder_5_out17, decoder_5_out18, decoder_5_out19, decoder_5_out20, decoder_5_out21,
       decoder_5_out22, decoder_5_out23, decoder_5_out24, decoder_5_out25, decoder_5_out26, decoder_5_out27,
       decoder_5_out28, decoder_5_out29, decoder_5_out30, decoder_5_out31, decoder_6_out0, decoder_6_out1,
       decoder_6_out2, decoder_6_out3, decoder_6_out4, decoder_6_out5, decoder_6_out6, decoder_6_out7,
       decoder_6_out8, decoder_6_out9, decoder_6_out10, decoder_6_out11, decoder_6_out12, decoder_6_out13,
       decoder_6_out14, decoder_6_out15, decoder_6_out16, decoder_6_out17, decoder_6_out18, decoder_6_out19,
       decoder_6_out20, decoder_6_out21, decoder_6_out22, decoder_6_out23, decoder_6_out24, decoder_6_out25,
       decoder_6_out26, decoder_6_out27, decoder_6_out28, decoder_6_out29, decoder_6_out30, decoder_6_out31,
       decoder_7_out0, decoder_7_out1, decoder_7_out2, decoder_7_out3, decoder_7_out4, decoder_7_out5,
       decoder_7_out6, decoder_7_out7, decoder_7_out8, decoder_7_out9, decoder_7_out10, decoder_7_out11,
       decoder_7_out12, decoder_7_out13, decoder_7_out14, decoder_7_out15, decoder_7_out16, decoder_7_out17,
       decoder_7_out18, decoder_7_out19, decoder_7_out20, decoder_7_out21, decoder_7_out22, decoder_7_out23,
       decoder_7_out24, decoder_7_out25, decoder_7_out26, decoder_7_out27, decoder_7_out28, decoder_7_out29,
       decoder_7_out30, decoder_7_out31, decoder_8_out0, decoder_8_out1, decoder_8_out2, decoder_8_out3,
       decoder_8_out4, decoder_8_out5, decoder_8_out6, decoder_8_out7, decoder_8_out8, decoder_8_out9,
       decoder_8_out10, decoder_8_out11, decoder_8_out12, decoder_8_out13, decoder_8_out14, decoder_8_out15,
       decoder_8_out16, decoder_8_out17, decoder_8_out18, decoder_8_out19, decoder_8_out20, decoder_8_out21,
       decoder_8_out22, decoder_8_out23, decoder_8_out24, decoder_8_out25, decoder_8_out26, decoder_8_out27,
       decoder_8_out28, decoder_8_out29, decoder_8_out30, decoder_8_out31, decoder_9_out0, decoder_9_out1,
       decoder_9_out2, decoder_9_out3, decoder_9_out4, decoder_9_out5, decoder_9_out6, decoder_9_out7,
       decoder_9_out8, decoder_9_out9, decoder_9_out10, decoder_9_out11, decoder_9_out12, decoder_9_out13,
       decoder_9_out14, decoder_9_out15, decoder_9_out16, decoder_9_out17, decoder_9_out18, decoder_9_out19,
       decoder_9_out20, decoder_9_out21, decoder_9_out22, decoder_9_out23, decoder_9_out24, decoder_9_out25,
       decoder_9_out26, decoder_9_out27, decoder_9_out28, decoder_9_out29, decoder_9_out30, decoder_9_out31;
  wire [31:0] n32_mem_modules_1_data_out, n32_mem_modules_2_data_out, n32_mem_modules_3_data_out,
       n32_mem_modules_4_data_out, n32_mem_modules_5_data_out, n32_mem_modules_6_data_out,
       n32_mem_modules_7_data_out, n32_mem_modules_8_data_out;

  Decoder #(.select(3)) decoder_1 (
    .out0(decoder_1_out0), .out1(decoder_1_out1), .out2(decoder_1_out2), .out3(decoder_1_out3),
    .out4(decoder_1_out4), .out5(decoder_1_out5), .out6(decoder_1_out6), .out7(decoder_1_out7),
    .sel(Address[26:24]));  // open: en
  Decoder #(.select(5)) decoder_2 (
    .out0(decoder_2_out0), .out1(decoder_2_out1), .out2(decoder_2_out2), .out3(decoder_2_out3),
    .out4(decoder_2_out4), .out5(decoder_2_out5), .out6(decoder_2_out6), .out7(decoder_2_out7),
    .out8(decoder_2_out8), .out9(decoder_2_out9), .out10(decoder_2_out10), .out11(decoder_2_out11),
    .out12(decoder_2_out12), .out13(decoder_2_out13), .out14(decoder_2_out14), .out15(decoder_2_out15),
    .out16(decoder_2_out16), .out17(decoder_2_out17), .out18(decoder_2_out18), .out19(decoder_2_out19),
    .out20(decoder_2_out20), .out21(decoder_2_out21), .out22(decoder_2_out22), .out23(decoder_2_out23),
    .out24(decoder_2_out24), .out25(decoder_2_out25), .out26(decoder_2_out26), .out27(decoder_2_out27),
    .out28(decoder_2_out28), .out29(decoder_2_out29), .out30(decoder_2_out30), .out31(decoder_2_out31),
    .sel(Address[31:27]), .en(decoder_1_out0));
  Decoder #(.select(5)) decoder_3 (
    .out0(decoder_3_out0), .out1(decoder_3_out1), .out2(decoder_3_out2), .out3(decoder_3_out3),
    .out4(decoder_3_out4), .out5(decoder_3_out5), .out6(decoder_3_out6), .out7(decoder_3_out7),
    .out8(decoder_3_out8), .out9(decoder_3_out9), .out10(decoder_3_out10), .out11(decoder_3_out11),
    .out12(decoder_3_out12), .out13(decoder_3_out13), .out14(decoder_3_out14), .out15(decoder_3_out15),
    .out16(decoder_3_out16), .out17(decoder_3_out17), .out18(decoder_3_out18), .out19(decoder_3_out19),
    .out20(decoder_3_out20), .out21(decoder_3_out21), .out22(decoder_3_out22), .out23(decoder_3_out23),
    .out24(decoder_3_out24), .out25(decoder_3_out25), .out26(decoder_3_out26), .out27(decoder_3_out27),
    .out28(decoder_3_out28), .out29(decoder_3_out29), .out30(decoder_3_out30), .out31(decoder_3_out31),
    .sel(Address[31:27]), .en(decoder_1_out1));
  Decoder #(.select(5)) decoder_4 (
    .out0(decoder_4_out0), .out1(decoder_4_out1), .out2(decoder_4_out2), .out3(decoder_4_out3),
    .out4(decoder_4_out4), .out5(decoder_4_out5), .out6(decoder_4_out6), .out7(decoder_4_out7),
    .out8(decoder_4_out8), .out9(decoder_4_out9), .out10(decoder_4_out10), .out11(decoder_4_out11),
    .out12(decoder_4_out12), .out13(decoder_4_out13), .out14(decoder_4_out14), .out15(decoder_4_out15),
    .out16(decoder_4_out16), .out17(decoder_4_out17), .out18(decoder_4_out18), .out19(decoder_4_out19),
    .out20(decoder_4_out20), .out21(decoder_4_out21), .out22(decoder_4_out22), .out23(decoder_4_out23),
    .out24(decoder_4_out24), .out25(decoder_4_out25), .out26(decoder_4_out26), .out27(decoder_4_out27),
    .out28(decoder_4_out28), .out29(decoder_4_out29), .out30(decoder_4_out30), .out31(decoder_4_out31),
    .sel(Address[31:27]), .en(decoder_1_out2));
  Decoder #(.select(5)) decoder_5 (
    .out0(decoder_5_out0), .out1(decoder_5_out1), .out2(decoder_5_out2), .out3(decoder_5_out3),
    .out4(decoder_5_out4), .out5(decoder_5_out5), .out6(decoder_5_out6), .out7(decoder_5_out7),
    .out8(decoder_5_out8), .out9(decoder_5_out9), .out10(decoder_5_out10), .out11(decoder_5_out11),
    .out12(decoder_5_out12), .out13(decoder_5_out13), .out14(decoder_5_out14), .out15(decoder_5_out15),
    .out16(decoder_5_out16), .out17(decoder_5_out17), .out18(decoder_5_out18), .out19(decoder_5_out19),
    .out20(decoder_5_out20), .out21(decoder_5_out21), .out22(decoder_5_out22), .out23(decoder_5_out23),
    .out24(decoder_5_out24), .out25(decoder_5_out25), .out26(decoder_5_out26), .out27(decoder_5_out27),
    .out28(decoder_5_out28), .out29(decoder_5_out29), .out30(decoder_5_out30), .out31(decoder_5_out31),
    .sel(Address[31:27]), .en(decoder_1_out3));
  Decoder #(.select(5)) decoder_6 (
    .out0(decoder_6_out0), .out1(decoder_6_out1), .out2(decoder_6_out2), .out3(decoder_6_out3),
    .out4(decoder_6_out4), .out5(decoder_6_out5), .out6(decoder_6_out6), .out7(decoder_6_out7),
    .out8(decoder_6_out8), .out9(decoder_6_out9), .out10(decoder_6_out10), .out11(decoder_6_out11),
    .out12(decoder_6_out12), .out13(decoder_6_out13), .out14(decoder_6_out14), .out15(decoder_6_out15),
    .out16(decoder_6_out16), .out17(decoder_6_out17), .out18(decoder_6_out18), .out19(decoder_6_out19),
    .out20(decoder_6_out20), .out21(decoder_6_out21), .out22(decoder_6_out22), .out23(decoder_6_out23),
    .out24(decoder_6_out24), .out25(decoder_6_out25), .out26(decoder_6_out26), .out27(decoder_6_out27),
    .out28(decoder_6_out28), .out29(decoder_6_out29), .out30(decoder_6_out30), .out31(decoder_6_out31),
    .sel(Address[31:27]), .en(decoder_1_out4));
  Decoder #(.select(5)) decoder_7 (
    .out0(decoder_7_out0), .out1(decoder_7_out1), .out2(decoder_7_out2), .out3(decoder_7_out3),
    .out4(decoder_7_out4), .out5(decoder_7_out5), .out6(decoder_7_out6), .out7(decoder_7_out7),
    .out8(decoder_7_out8), .out9(decoder_7_out9), .out10(decoder_7_out10), .out11(decoder_7_out11),
    .out12(decoder_7_out12), .out13(decoder_7_out13), .out14(decoder_7_out14), .out15(decoder_7_out15),
    .out16(decoder_7_out16), .out17(decoder_7_out17), .out18(decoder_7_out18), .out19(decoder_7_out19),
    .out20(decoder_7_out20), .out21(decoder_7_out21), .out22(decoder_7_out22), .out23(decoder_7_out23),
    .out24(decoder_7_out24), .out25(decoder_7_out25), .out26(decoder_7_out26), .out27(decoder_7_out27),
    .out28(decoder_7_out28), .out29(decoder_7_out29), .out30(decoder_7_out30), .out31(decoder_7_out31),
    .sel(Address[31:27]), .en(decoder_1_out5));
  Decoder #(.select(5)) decoder_8 (
    .out0(decoder_8_out0), .out1(decoder_8_out1), .out2(decoder_8_out2), .out3(decoder_8_out3),
    .out4(decoder_8_out4), .out5(decoder_8_out5), .out6(decoder_8_out6), .out7(decoder_8_out7),
    .out8(decoder_8_out8), .out9(decoder_8_out9), .out10(decoder_8_out10), .out11(decoder_8_out11),
    .out12(decoder_8_out12), .out13(decoder_8_out13), .out14(decoder_8_out14), .out15(decoder_8_out15),
    .out16(decoder_8_out16), .out17(decoder_8_out17), .out18(decoder_8_out18), .out19(decoder_8_out19),
    .out20(decoder_8_out20), .out21(decoder_8_out21), .out22(decoder_8_out22), .out23(decoder_8_out23),
    .out24(decoder_8_out24), .out25(decoder_8_out25), .out26(decoder_8_out26), .out27(decoder_8_out27),
    .out28(decoder_8_out28), .out29(decoder_8_out29), .out30(decoder_8_out30), .out31(decoder_8_out31),
    .sel(Address[31:27]), .en(decoder_1_out6));
  Decoder #(.select(5)) decoder_9 (
    .out0(decoder_9_out0), .out1(decoder_9_out1), .out2(decoder_9_out2), .out3(decoder_9_out3),
    .out4(decoder_9_out4), .out5(decoder_9_out5), .out6(decoder_9_out6), .out7(decoder_9_out7),
    .out8(decoder_9_out8), .out9(decoder_9_out9), .out10(decoder_9_out10), .out11(decoder_9_out11),
    .out12(decoder_9_out12), .out13(decoder_9_out13), .out14(decoder_9_out14), .out15(decoder_9_out15),
    .out16(decoder_9_out16), .out17(decoder_9_out17), .out18(decoder_9_out18), .out19(decoder_9_out19),
    .out20(decoder_9_out20), .out21(decoder_9_out21), .out22(decoder_9_out22), .out23(decoder_9_out23),
    .out24(decoder_9_out24), .out25(decoder_9_out25), .out26(decoder_9_out26), .out27(decoder_9_out27),
    .out28(decoder_9_out28), .out29(decoder_9_out29), .out30(decoder_9_out30), .out31(decoder_9_out31),
    .sel(Address[31:27]), .en(decoder_1_out7));
  _32_Mem_Modules u_32_mem_modules_1 (
    .Addr(Address[23:0]), ._1(decoder_2_out0), .MemWrite(MemWrite), .MemRead(MemRead), .Data_In(Data_In),
    ._2(decoder_2_out1), ._3(decoder_2_out2), ._4(decoder_2_out3), ._5(decoder_2_out4), ._6(decoder_2_out5),
    ._7(decoder_2_out6), ._8(decoder_2_out7), ._9(decoder_2_out8), ._10(decoder_2_out9),
    ._11(decoder_2_out10), ._12(decoder_2_out11), ._13(decoder_2_out12), ._14(decoder_2_out13),
    ._15(decoder_2_out14), ._16(decoder_2_out15), ._17(decoder_2_out16), ._18(decoder_2_out17),
    ._19(decoder_2_out18), ._20(decoder_2_out19), ._21(decoder_2_out20), ._22(decoder_2_out21),
    ._23(decoder_2_out22), ._24(decoder_2_out23), ._25(decoder_2_out24), ._26(decoder_2_out25),
    ._27(decoder_2_out26), ._28(decoder_2_out27), ._29(decoder_2_out28), ._30(decoder_2_out29),
    ._31(decoder_2_out30), ._32(decoder_2_out31), .Data_Out(n32_mem_modules_1_data_out), .Clk(Clk));
  _32_Mem_Modules u_32_mem_modules_2 (
    .Addr(Address[23:0]), ._1(decoder_3_out0), .MemWrite(MemWrite), .MemRead(MemRead), .Data_In(Data_In),
    ._2(decoder_3_out1), ._3(decoder_3_out2), ._4(decoder_3_out3), ._5(decoder_3_out4), ._6(decoder_3_out5),
    ._7(decoder_3_out6), ._8(decoder_3_out7), ._9(decoder_3_out8), ._10(decoder_3_out9),
    ._11(decoder_3_out10), ._12(decoder_3_out11), ._13(decoder_3_out12), ._14(decoder_3_out13),
    ._15(decoder_3_out14), ._16(decoder_3_out15), ._17(decoder_3_out16), ._18(decoder_3_out17),
    ._19(decoder_3_out18), ._20(decoder_3_out19), ._21(decoder_3_out20), ._22(decoder_3_out21),
    ._23(decoder_3_out22), ._24(decoder_3_out23), ._25(decoder_3_out24), ._26(decoder_3_out25),
    ._27(decoder_3_out26), ._28(decoder_3_out27), ._29(decoder_3_out28), ._30(decoder_3_out29),
    ._31(decoder_3_out30), ._32(decoder_3_out31), .Data_Out(n32_mem_modules_2_data_out), .Clk(Clk));
  _32_Mem_Modules u_32_mem_modules_3 (
    .Addr(Address[23:0]), ._1(decoder_4_out0), .MemWrite(MemWrite), .MemRead(MemRead), .Data_In(Data_In),
    ._2(decoder_4_out1), ._3(decoder_4_out2), ._4(decoder_4_out3), ._5(decoder_4_out4), ._6(decoder_4_out5),
    ._7(decoder_4_out6), ._8(decoder_4_out7), ._9(decoder_4_out8), ._10(decoder_4_out9),
    ._11(decoder_4_out10), ._12(decoder_4_out11), ._13(decoder_4_out12), ._14(decoder_4_out13),
    ._15(decoder_4_out14), ._16(decoder_4_out15), ._17(decoder_4_out16), ._18(decoder_4_out17),
    ._19(decoder_4_out18), ._20(decoder_4_out19), ._21(decoder_4_out20), ._22(decoder_4_out21),
    ._23(decoder_4_out22), ._24(decoder_4_out23), ._25(decoder_4_out24), ._26(decoder_4_out25),
    ._27(decoder_4_out26), ._28(decoder_4_out27), ._29(decoder_4_out28), ._30(decoder_4_out29),
    ._31(decoder_4_out30), ._32(decoder_4_out31), .Data_Out(n32_mem_modules_3_data_out), .Clk(Clk));
  _32_Mem_Modules u_32_mem_modules_4 (
    .Addr(Address[23:0]), ._1(decoder_5_out0), .MemWrite(MemWrite), .MemRead(MemRead), .Data_In(Data_In),
    ._2(decoder_5_out1), ._3(decoder_5_out2), ._4(decoder_5_out3), ._5(decoder_5_out4), ._6(decoder_5_out5),
    ._7(decoder_5_out6), ._8(decoder_5_out7), ._9(decoder_5_out8), ._10(decoder_5_out9),
    ._11(decoder_5_out10), ._12(decoder_5_out11), ._13(decoder_5_out12), ._14(decoder_5_out13),
    ._15(decoder_5_out14), ._16(decoder_5_out15), ._17(decoder_5_out16), ._18(decoder_5_out17),
    ._19(decoder_5_out18), ._20(decoder_5_out19), ._21(decoder_5_out20), ._22(decoder_5_out21),
    ._23(decoder_5_out22), ._24(decoder_5_out23), ._25(decoder_5_out24), ._26(decoder_5_out25),
    ._27(decoder_5_out26), ._28(decoder_5_out27), ._29(decoder_5_out28), ._30(decoder_5_out29),
    ._31(decoder_5_out30), ._32(decoder_5_out31), .Data_Out(n32_mem_modules_4_data_out), .Clk(Clk));
  _32_Mem_Modules u_32_mem_modules_5 (
    .Addr(Address[23:0]), ._1(decoder_6_out0), .MemWrite(MemWrite), .MemRead(MemRead), .Data_In(Data_In),
    ._2(decoder_6_out1), ._3(decoder_6_out2), ._4(decoder_6_out3), ._5(decoder_6_out4), ._6(decoder_6_out5),
    ._7(decoder_6_out6), ._8(decoder_6_out7), ._9(decoder_6_out8), ._10(decoder_6_out9),
    ._11(decoder_6_out10), ._12(decoder_6_out11), ._13(decoder_6_out12), ._14(decoder_6_out13),
    ._15(decoder_6_out14), ._16(decoder_6_out15), ._17(decoder_6_out16), ._18(decoder_6_out17),
    ._19(decoder_6_out18), ._20(decoder_6_out19), ._21(decoder_6_out20), ._22(decoder_6_out21),
    ._23(decoder_6_out22), ._24(decoder_6_out23), ._25(decoder_6_out24), ._26(decoder_6_out25),
    ._27(decoder_6_out26), ._28(decoder_6_out27), ._29(decoder_6_out28), ._30(decoder_6_out29),
    ._31(decoder_6_out30), ._32(decoder_6_out31), .Data_Out(n32_mem_modules_5_data_out), .Clk(Clk));
  _32_Mem_Modules u_32_mem_modules_6 (
    .Addr(Address[23:0]), ._1(decoder_7_out0), .MemWrite(MemWrite), .MemRead(MemRead), .Data_In(Data_In),
    ._2(decoder_7_out1), ._3(decoder_7_out2), ._4(decoder_7_out3), ._5(decoder_7_out4), ._6(decoder_7_out5),
    ._7(decoder_7_out6), ._8(decoder_7_out7), ._9(decoder_7_out8), ._10(decoder_7_out9),
    ._11(decoder_7_out10), ._12(decoder_7_out11), ._13(decoder_7_out12), ._14(decoder_7_out13),
    ._15(decoder_7_out14), ._16(decoder_7_out15), ._17(decoder_7_out16), ._18(decoder_7_out17),
    ._19(decoder_7_out18), ._20(decoder_7_out19), ._21(decoder_7_out20), ._22(decoder_7_out21),
    ._23(decoder_7_out22), ._24(decoder_7_out23), ._25(decoder_7_out24), ._26(decoder_7_out25),
    ._27(decoder_7_out26), ._28(decoder_7_out27), ._29(decoder_7_out28), ._30(decoder_7_out29),
    ._31(decoder_7_out30), ._32(decoder_7_out31), .Data_Out(n32_mem_modules_6_data_out), .Clk(Clk));
  _32_Mem_Modules u_32_mem_modules_7 (
    .Addr(Address[23:0]), ._1(decoder_8_out0), .MemWrite(MemWrite), .MemRead(MemRead), .Data_In(Data_In),
    ._2(decoder_8_out1), ._3(decoder_8_out2), ._4(decoder_8_out3), ._5(decoder_8_out4), ._6(decoder_8_out5),
    ._7(decoder_8_out6), ._8(decoder_8_out7), ._9(decoder_8_out8), ._10(decoder_8_out9),
    ._11(decoder_8_out10), ._12(decoder_8_out11), ._13(decoder_8_out12), ._14(decoder_8_out13),
    ._15(decoder_8_out14), ._16(decoder_8_out15), ._17(decoder_8_out16), ._18(decoder_8_out17),
    ._19(decoder_8_out18), ._20(decoder_8_out19), ._21(decoder_8_out20), ._22(decoder_8_out21),
    ._23(decoder_8_out22), ._24(decoder_8_out23), ._25(decoder_8_out24), ._26(decoder_8_out25),
    ._27(decoder_8_out26), ._28(decoder_8_out27), ._29(decoder_8_out28), ._30(decoder_8_out29),
    ._31(decoder_8_out30), ._32(decoder_8_out31), .Data_Out(n32_mem_modules_7_data_out), .Clk(Clk));
  _32_Mem_Modules u_32_mem_modules_8 (
    .Addr(Address[23:0]), ._1(decoder_9_out0), .MemWrite(MemWrite), .MemRead(MemRead), .Data_In(Data_In),
    ._2(decoder_9_out1), ._3(decoder_9_out2), ._4(decoder_9_out3), ._5(decoder_9_out4), ._6(decoder_9_out5),
    ._7(decoder_9_out6), ._8(decoder_9_out7), ._9(decoder_9_out8), ._10(decoder_9_out9),
    ._11(decoder_9_out10), ._12(decoder_9_out11), ._13(decoder_9_out12), ._14(decoder_9_out13),
    ._15(decoder_9_out14), ._16(decoder_9_out15), ._17(decoder_9_out16), ._18(decoder_9_out17),
    ._19(decoder_9_out18), ._20(decoder_9_out19), ._21(decoder_9_out20), ._22(decoder_9_out21),
    ._23(decoder_9_out22), ._24(decoder_9_out23), ._25(decoder_9_out24), ._26(decoder_9_out25),
    ._27(decoder_9_out26), ._28(decoder_9_out27), ._29(decoder_9_out28), ._30(decoder_9_out29),
    ._31(decoder_9_out30), ._32(decoder_9_out31), .Data_Out(n32_mem_modules_8_data_out), .Clk(Clk));
  assign Data_Out = n32_mem_modules_1_data_out | n32_mem_modules_2_data_out | n32_mem_modules_3_data_out | n32_mem_modules_4_data_out | n32_mem_modules_5_data_out | n32_mem_modules_6_data_out | n32_mem_modules_7_data_out | n32_mem_modules_8_data_out;  // OR_Gate or_1, 32 bits wide

  // Notes on the sheet:
  //   LOWEST_ORDER ADDRESSES HERE
endmodule

module helper (
  input  in_1,
  output [31:0] out_2
);


  assign out_2 = {32{in_1}};
endmodule

module _32_Mem_Modules (
  input  Clk,
  input  [23:0] Addr,
  input  _1,
  input  MemWrite,
  input  MemRead,
  input  [31:0] Data_In,
  input  _2,
  input  _3,
  input  _4,
  input  _5,
  input  _6,
  input  _7,
  input  _8,
  input  _9,
  input  _10,
  input  _11,
  input  _12,
  input  _13,
  input  _14,
  input  _15,
  input  _16,
  input  _17,
  input  _18,
  input  _19,
  input  _20,
  input  _21,
  input  _22,
  input  _23,
  input  _24,
  input  _25,
  input  _26,
  input  _27,
  input  _28,
  input  _29,
  input  _30,
  input  _31,
  input  _32,
  output [31:0] Data_Out
);

  wire [31:0] and_1_out, and_2_out, and_3_out, and_4_out, and_5_out, and_6_out, and_7_out, and_8_out,
       and_9_out, and_10_out, and_11_out, and_12_out, and_13_out, and_14_out, and_15_out, and_16_out,
       and_17_out, and_18_out, and_19_out, and_20_out, and_21_out, and_22_out, and_23_out, and_24_out,
       and_25_out, and_26_out, and_27_out, and_28_out, and_29_out, and_30_out, and_31_out, and_32_out,
       helper_1_out_2, helper_2_out_2, helper_3_out_2, helper_4_out_2, helper_5_out_2, helper_6_out_2,
       helper_7_out_2, helper_8_out_2, helper_9_out_2, helper_10_out_2, helper_11_out_2, helper_12_out_2,
       helper_13_out_2, helper_14_out_2, helper_15_out_2, helper_16_out_2, helper_17_out_2, helper_18_out_2,
       helper_19_out_2, helper_20_out_2, helper_21_out_2, helper_22_out_2, helper_23_out_2, helper_24_out_2,
       helper_25_out_2, helper_26_out_2, helper_27_out_2, helper_28_out_2, helper_29_out_2, helper_30_out_2,
       helper_31_out_2, helper_32_out_2, ram_1_data, ram_2_data, ram_3_data, ram_4_data, ram_5_data,
       ram_6_data, ram_7_data, ram_8_data, ram_9_data, ram_10_data, ram_11_data, ram_12_data, ram_13_data,
       ram_14_data, ram_15_data, ram_16_data, ram_17_data, ram_18_data, ram_19_data, ram_20_data,
       ram_21_data, ram_22_data, ram_23_data, ram_24_data, ram_25_data, ram_26_data, ram_27_data,
       ram_28_data, ram_29_data, ram_30_data, ram_31_data, ram_32_data;

  RAM #(.addrWidth(24), .dataWidth(32), .bus("separate")) ram_1 (
    .addr(Addr), .din(Data_In), .data(ram_1_data), .str(MemWrite), .sel(_1), .clk(Clk), .ld(MemRead));  // open: clr
  RAM #(.addrWidth(24), .dataWidth(32), .bus("separate")) ram_2 (
    .addr(Addr), .din(Data_In), .data(ram_2_data), .str(MemWrite), .sel(_2), .clk(Clk), .ld(MemRead));  // open: clr
  RAM #(.addrWidth(24), .dataWidth(32), .bus("separate")) ram_3 (
    .addr(Addr), .din(Data_In), .data(ram_3_data), .str(MemWrite), .sel(_3), .clk(Clk), .ld(MemRead));  // open: clr
  RAM #(.addrWidth(24), .dataWidth(32), .bus("separate")) ram_4 (
    .addr(Addr), .din(Data_In), .data(ram_4_data), .str(MemWrite), .sel(_4), .clk(Clk), .ld(MemRead));  // open: clr
  RAM #(.addrWidth(24), .dataWidth(32), .bus("separate")) ram_5 (
    .addr(Addr), .din(Data_In), .data(ram_5_data), .str(MemWrite), .sel(_5), .clk(Clk), .ld(MemRead));  // open: clr
  RAM #(.addrWidth(24), .dataWidth(32), .bus("separate")) ram_6 (
    .addr(Addr), .din(Data_In), .data(ram_6_data), .str(MemWrite), .sel(_6), .clk(Clk), .ld(MemRead));  // open: clr
  RAM #(.addrWidth(24), .dataWidth(32), .bus("separate")) ram_7 (
    .addr(Addr), .din(Data_In), .data(ram_7_data), .str(MemWrite), .sel(_7), .clk(Clk), .ld(MemRead));  // open: clr
  RAM #(.addrWidth(24), .dataWidth(32), .bus("separate")) ram_8 (
    .addr(Addr), .din(Data_In), .data(ram_8_data), .str(MemWrite), .sel(_8), .clk(Clk), .ld(MemRead));  // open: clr
  RAM #(.addrWidth(24), .dataWidth(32), .bus("separate")) ram_9 (
    .addr(Addr), .din(Data_In), .data(ram_9_data), .str(MemWrite), .sel(_9), .clk(Clk), .ld(MemRead));  // open: clr
  RAM #(.addrWidth(24), .dataWidth(32), .bus("separate")) ram_10 (
    .addr(Addr), .din(Data_In), .data(ram_10_data), .str(MemWrite), .sel(_10), .clk(Clk), .ld(MemRead));  // open: clr
  RAM #(.addrWidth(24), .dataWidth(32), .bus("separate")) ram_11 (
    .addr(Addr), .din(Data_In), .data(ram_11_data), .str(MemWrite), .sel(_11), .clk(Clk), .ld(MemRead));  // open: clr
  RAM #(.addrWidth(24), .dataWidth(32), .bus("separate")) ram_12 (
    .addr(Addr), .din(Data_In), .data(ram_12_data), .str(MemWrite), .sel(_12), .clk(Clk), .ld(MemRead));  // open: clr
  RAM #(.addrWidth(24), .dataWidth(32), .bus("separate")) ram_13 (
    .addr(Addr), .din(Data_In), .data(ram_13_data), .str(MemWrite), .sel(_13), .clk(Clk), .ld(MemRead));  // open: clr
  RAM #(.addrWidth(24), .dataWidth(32), .bus("separate")) ram_14 (
    .addr(Addr), .din(Data_In), .data(ram_14_data), .str(MemWrite), .sel(_14), .clk(Clk), .ld(MemRead));  // open: clr
  RAM #(.addrWidth(24), .dataWidth(32), .bus("separate")) ram_15 (
    .addr(Addr), .din(Data_In), .data(ram_15_data), .str(MemWrite), .sel(_15), .clk(Clk), .ld(MemRead));  // open: clr
  RAM #(.addrWidth(24), .dataWidth(32), .bus("separate")) ram_16 (
    .addr(Addr), .din(Data_In), .data(ram_16_data), .str(MemWrite), .sel(_16), .clk(Clk), .ld(MemRead));  // open: clr
  RAM #(.addrWidth(24), .dataWidth(32), .bus("separate")) ram_17 (
    .addr(Addr), .din(Data_In), .data(ram_17_data), .str(MemWrite), .sel(_17), .clk(Clk), .ld(MemRead));  // open: clr
  RAM #(.addrWidth(24), .dataWidth(32), .bus("separate")) ram_18 (
    .addr(Addr), .din(Data_In), .data(ram_18_data), .str(MemWrite), .sel(_18), .clk(Clk), .ld(MemRead));  // open: clr
  RAM #(.addrWidth(24), .dataWidth(32), .bus("separate")) ram_19 (
    .addr(Addr), .din(Data_In), .data(ram_19_data), .str(MemWrite), .sel(_19), .clk(Clk), .ld(MemRead));  // open: clr
  RAM #(.addrWidth(24), .dataWidth(32), .bus("separate")) ram_20 (
    .addr(Addr), .din(Data_In), .data(ram_20_data), .str(MemWrite), .sel(_20), .clk(Clk), .ld(MemRead));  // open: clr
  RAM #(.addrWidth(24), .dataWidth(32), .bus("separate")) ram_21 (
    .addr(Addr), .din(Data_In), .data(ram_21_data), .str(MemWrite), .sel(_21), .clk(Clk), .ld(MemRead));  // open: clr
  RAM #(.addrWidth(24), .dataWidth(32), .bus("separate")) ram_22 (
    .addr(Addr), .din(Data_In), .data(ram_22_data), .str(MemWrite), .sel(_22), .clk(Clk), .ld(MemRead));  // open: clr
  RAM #(.addrWidth(24), .dataWidth(32), .bus("separate")) ram_23 (
    .addr(Addr), .din(Data_In), .data(ram_23_data), .str(MemWrite), .sel(_23), .clk(Clk), .ld(MemRead));  // open: clr
  RAM #(.addrWidth(24), .dataWidth(32), .bus("separate")) ram_24 (
    .addr(Addr), .din(Data_In), .data(ram_24_data), .str(MemWrite), .sel(_24), .clk(Clk), .ld(MemRead));  // open: clr
  RAM #(.addrWidth(24), .dataWidth(32), .bus("separate")) ram_25 (
    .addr(Addr), .din(Data_In), .data(ram_25_data), .str(MemWrite), .sel(_25), .clk(Clk), .ld(MemRead));  // open: clr
  RAM #(.addrWidth(24), .dataWidth(32), .bus("separate")) ram_26 (
    .addr(Addr), .din(Data_In), .data(ram_26_data), .str(MemWrite), .sel(_26), .clk(Clk), .ld(MemRead));  // open: clr
  RAM #(.addrWidth(24), .dataWidth(32), .bus("separate")) ram_27 (
    .addr(Addr), .din(Data_In), .data(ram_27_data), .str(MemWrite), .sel(_27), .clk(Clk), .ld(MemRead));  // open: clr
  RAM #(.addrWidth(24), .dataWidth(32), .bus("separate")) ram_28 (
    .addr(Addr), .din(Data_In), .data(ram_28_data), .str(MemWrite), .sel(_28), .clk(Clk), .ld(MemRead));  // open: clr
  RAM #(.addrWidth(24), .dataWidth(32), .bus("separate")) ram_29 (
    .addr(Addr), .din(Data_In), .data(ram_29_data), .str(MemWrite), .sel(_29), .clk(Clk), .ld(MemRead));  // open: clr
  RAM #(.addrWidth(24), .dataWidth(32), .bus("separate")) ram_30 (
    .addr(Addr), .din(Data_In), .data(ram_30_data), .str(MemWrite), .sel(_30), .clk(Clk), .ld(MemRead));  // open: clr
  RAM #(.addrWidth(24), .dataWidth(32), .bus("separate")) ram_31 (
    .addr(Addr), .din(Data_In), .data(ram_31_data), .str(MemWrite), .sel(_31), .clk(Clk), .ld(MemRead));  // open: clr
  RAM #(.addrWidth(24), .dataWidth(32), .bus("separate")) ram_32 (
    .addr(Addr), .din(Data_In), .data(ram_32_data), .str(MemWrite), .sel(_32), .clk(Clk), .ld(MemRead));  // open: clr
  helper helper_1 (.in_1(_1), .out_2(helper_1_out_2));
  helper helper_2 (.in_1(_2), .out_2(helper_2_out_2));
  helper helper_3 (.in_1(_3), .out_2(helper_3_out_2));
  helper helper_4 (.in_1(_4), .out_2(helper_4_out_2));
  helper helper_5 (.in_1(_5), .out_2(helper_5_out_2));
  helper helper_6 (.in_1(_6), .out_2(helper_6_out_2));
  helper helper_7 (.in_1(_7), .out_2(helper_7_out_2));
  helper helper_8 (.in_1(_8), .out_2(helper_8_out_2));
  helper helper_9 (.in_1(_9), .out_2(helper_9_out_2));
  helper helper_10 (.in_1(_10), .out_2(helper_10_out_2));
  helper helper_11 (.in_1(_11), .out_2(helper_11_out_2));
  helper helper_12 (.in_1(_12), .out_2(helper_12_out_2));
  helper helper_13 (.in_1(_13), .out_2(helper_13_out_2));
  helper helper_14 (.in_1(_14), .out_2(helper_14_out_2));
  helper helper_15 (.in_1(_15), .out_2(helper_15_out_2));
  helper helper_16 (.in_1(_16), .out_2(helper_16_out_2));
  helper helper_17 (.in_1(_17), .out_2(helper_17_out_2));
  helper helper_18 (.in_1(_18), .out_2(helper_18_out_2));
  helper helper_19 (.in_1(_19), .out_2(helper_19_out_2));
  helper helper_20 (.in_1(_20), .out_2(helper_20_out_2));
  helper helper_21 (.in_1(_21), .out_2(helper_21_out_2));
  helper helper_22 (.in_1(_22), .out_2(helper_22_out_2));
  helper helper_23 (.in_1(_23), .out_2(helper_23_out_2));
  helper helper_24 (.in_1(_24), .out_2(helper_24_out_2));
  helper helper_25 (.in_1(_25), .out_2(helper_25_out_2));
  helper helper_26 (.in_1(_26), .out_2(helper_26_out_2));
  helper helper_27 (.in_1(_27), .out_2(helper_27_out_2));
  helper helper_28 (.in_1(_28), .out_2(helper_28_out_2));
  helper helper_29 (.in_1(_29), .out_2(helper_29_out_2));
  helper helper_30 (.in_1(_30), .out_2(helper_30_out_2));
  helper helper_31 (.in_1(_31), .out_2(helper_31_out_2));
  helper helper_32 (.in_1(_32), .out_2(helper_32_out_2));
  assign and_1_out = ram_1_data & helper_1_out_2;  // AND_Gate and_1, 32 bits wide
  assign and_2_out = ram_2_data & helper_2_out_2;  // AND_Gate and_2, 32 bits wide
  assign and_3_out = ram_3_data & helper_3_out_2;  // AND_Gate and_3, 32 bits wide
  assign and_4_out = ram_4_data & helper_4_out_2;  // AND_Gate and_4, 32 bits wide
  assign and_5_out = ram_5_data & helper_5_out_2;  // AND_Gate and_5, 32 bits wide
  assign and_6_out = ram_6_data & helper_6_out_2;  // AND_Gate and_6, 32 bits wide
  assign and_7_out = ram_7_data & helper_7_out_2;  // AND_Gate and_7, 32 bits wide
  assign and_8_out = ram_8_data & helper_8_out_2;  // AND_Gate and_8, 32 bits wide
  assign and_9_out = ram_9_data & helper_9_out_2;  // AND_Gate and_9, 32 bits wide
  assign and_10_out = ram_10_data & helper_10_out_2;  // AND_Gate and_10, 32 bits wide
  assign and_11_out = ram_11_data & helper_11_out_2;  // AND_Gate and_11, 32 bits wide
  assign and_12_out = ram_12_data & helper_12_out_2;  // AND_Gate and_12, 32 bits wide
  assign and_13_out = ram_13_data & helper_13_out_2;  // AND_Gate and_13, 32 bits wide
  assign and_14_out = ram_14_data & helper_14_out_2;  // AND_Gate and_14, 32 bits wide
  assign and_15_out = ram_15_data & helper_15_out_2;  // AND_Gate and_15, 32 bits wide
  assign and_16_out = ram_16_data & helper_16_out_2;  // AND_Gate and_16, 32 bits wide
  assign and_17_out = ram_17_data & helper_17_out_2;  // AND_Gate and_17, 32 bits wide
  assign and_18_out = ram_18_data & helper_18_out_2;  // AND_Gate and_18, 32 bits wide
  assign and_19_out = ram_19_data & helper_19_out_2;  // AND_Gate and_19, 32 bits wide
  assign and_20_out = ram_20_data & helper_20_out_2;  // AND_Gate and_20, 32 bits wide
  assign and_21_out = ram_21_data & helper_21_out_2;  // AND_Gate and_21, 32 bits wide
  assign and_22_out = ram_22_data & helper_22_out_2;  // AND_Gate and_22, 32 bits wide
  assign and_23_out = ram_23_data & helper_23_out_2;  // AND_Gate and_23, 32 bits wide
  assign and_24_out = ram_24_data & helper_24_out_2;  // AND_Gate and_24, 32 bits wide
  assign and_25_out = ram_25_data & helper_25_out_2;  // AND_Gate and_25, 32 bits wide
  assign and_26_out = ram_26_data & helper_26_out_2;  // AND_Gate and_26, 32 bits wide
  assign and_27_out = ram_27_data & helper_27_out_2;  // AND_Gate and_27, 32 bits wide
  assign and_28_out = ram_28_data & helper_28_out_2;  // AND_Gate and_28, 32 bits wide
  assign and_29_out = ram_29_data & helper_29_out_2;  // AND_Gate and_29, 32 bits wide
  assign and_30_out = ram_30_data & helper_30_out_2;  // AND_Gate and_30, 32 bits wide
  assign and_31_out = ram_31_data & helper_31_out_2;  // AND_Gate and_31, 32 bits wide
  assign and_32_out = ram_32_data & helper_32_out_2;  // AND_Gate and_32, 32 bits wide
  assign Data_Out = and_1_out | and_2_out | and_3_out | and_4_out | and_5_out | and_6_out | and_7_out | and_8_out | and_9_out | and_10_out | and_11_out | and_12_out | and_13_out | and_14_out | and_15_out | and_16_out | and_17_out | and_18_out | and_19_out | and_20_out | and_21_out | and_22_out | and_23_out | and_24_out | and_25_out | and_26_out | and_27_out | and_28_out | and_29_out | and_30_out | and_31_out | and_32_out;  // OR_Gate or_1, 32 bits wide

  // Notes on the sheet:
  //   SELECT
  //   SELECT
  //   SELECT
  //   SELECT
  //   SELECT
  //   SELECT
  //   SELECT
  //   SELECT
  //   SELECT
  //   SELECT
  //   SELECT
  //   SELECT
  //   SELECT
  //   SELECT
  //   SELECT
  //   SELECT
  //   SELECT
  //   SELECT
  //   SELECT
  //   SELECT
  //   SELECT
  //   SELECT
  //   SELECT
  //   SELECT
  //   SELECT
  //   SELECT
  //   SELECT
  //   SELECT
  //   SELECT
  //   SELECT
  //   SELECT
  //   Mem Module 1 (lower addresses)
endmodule
