// Logisim project ALUCTrl.circ as structural Verilog: 1 circuit, main circuit main
module main (
  input  [5:0] func,
  input  [2:0] ALUOp,
  output [3:0] out_3
);

  wire add, \and , and_1_out, and_2_out, and_3_out, and_4_out, and_5_out, and_6_out, comparator_8_eq,
       comparator_9_eq, comparator_10_eq, comparator_11_eq, comparator_12_eq, comparator_13_eq, en_op, \or ,
       or_1_out, or_2_out, or_3_out, or_4_out, or_5_out, or_6_out, slt, sub, \xor ;

  Comparator #(.width(3)) comparator_1 (.a(ALUOp), .b(3'b000), .eq(en_op));  // open: gt, lt
  Comparator #(.width(6)) comparator_2 (.a(func), .b(6'b100000), .eq(add));  // open: gt, lt
  Comparator #(.width(6)) comparator_3 (.a(func), .b(6'b100010), .eq(sub));  // open: gt, lt
  Comparator #(.width(6)) comparator_4 (.a(func), .b(6'b100100), .eq(\and ));  // open: gt, lt
  Comparator #(.width(6)) comparator_5 (.a(func), .b(6'b100101), .eq(\or ));  // open: gt, lt
  Comparator #(.width(6)) comparator_6 (.a(func), .b(6'b100110), .eq(\xor ));  // open: gt, lt
  Comparator #(.width(6)) comparator_7 (.a(func), .b(6'b101010), .eq(slt));  // open: gt, lt
  Comparator #(.width(3)) comparator_8 (.a(ALUOp), .b(3'b100), .eq(comparator_8_eq));  // open: gt, lt
  Comparator #(.width(3)) comparator_9 (.a(ALUOp), .b(3'b101), .eq(comparator_9_eq));  // open: gt, lt
  Comparator #(.width(3)) comparator_10 (.a(ALUOp), .b(3'b001), .eq(comparator_10_eq));  // open: gt, lt
  Comparator #(.width(3)) comparator_11 (.a(ALUOp), .b(3'b010), .eq(comparator_11_eq));  // open: gt, lt
  Comparator #(.width(3)) comparator_12 (.a(ALUOp), .b(3'b011), .eq(comparator_12_eq));  // open: gt, lt
  Comparator #(.width(3)) comparator_13 (.a(ALUOp), .b(3'b110), .eq(comparator_13_eq));  // open: gt, lt
  and and_1 (and_1_out, add, en_op);
  and and_2 (and_2_out, sub, en_op);
  and and_3 (and_3_out, \and , en_op);
  and and_4 (and_4_out, \or , en_op);
  and and_5 (and_5_out, \xor , en_op);
  and and_6 (and_6_out, slt, en_op);
  assign out_3 = or_1_out ? 4'b1100 : 4'bz;  // Controlled_Buffer controlled_buffer_1
  or or_1 (or_1_out, and_1_out, comparator_8_eq);
  or or_2 (or_2_out, comparator_9_eq, and_2_out);
  or or_3 (or_3_out, and_3_out, comparator_10_eq);
  or or_4 (or_4_out, and_4_out, comparator_11_eq);
  or or_5 (or_5_out, and_5_out, comparator_12_eq);
  or or_6 (or_6_out, and_6_out, comparator_13_eq);
  assign out_3 = or_2_out ? 4'b1101 : 4'bz;  // Controlled_Buffer controlled_buffer_2
  assign out_3 = or_3_out ? 4'b0001 : 4'bz;  // Controlled_Buffer controlled_buffer_3
  assign out_3 = or_4_out ? 4'b0010 : 4'bz;  // Controlled_Buffer controlled_buffer_4
  assign out_3 = or_5_out ? 4'b0011 : 4'bz;  // Controlled_Buffer controlled_buffer_5
  assign out_3 = or_6_out ? 4'b1110 : 4'bz;  // Controlled_Buffer controlled_buffer_6

  // Other names for the same wires on the sheet: F[5:0] = func; op[2:0] = ALUOp

  // Notes on the sheet:
  //   ADD
  //   SUB
  //   AND
  //   OR
  //   XOR
  //   SLT
endmodule
