// Logisim project ALU_Fixed.circ as structural Verilog: 6 circuits, main circuit ALU MAIN
module _1_bit_Adder (
  input  C_In,
  input  A,
  input  B,
  input  Arith__Op,
  output Sum,
  output C_Out
);

  wire or_1_out, xor_1_out;

  buf or_1 (or_1_out, C_In);  // OR_Gate
  xor xor_1 (xor_1_out, B, Arith__Op);
  Adder #(.width(1)) adder_1 (.a(A), .b(xor_1_out), .out(Sum), .cin(or_1_out), .cout(C_Out));
endmodule

module Shifter (
  input  [1:0] Shift_Rotate_Op,
  input  [4:0] Shift_Amount,
  input  [31:0] B,
  output [31:0] Shift_Result
);


  // Notes on the sheet:
  //   As a result the shifter isn't implemented.
  //   Turns out the shifter isn't necessary for the instruction set we must support.
endmodule

// Adder
module _32_bit_Adder (
  input  Arith__Op,
  input  [31:0] A,
  input  [31:0] B,
  output Overflow,
  output [31:0] Result
);

  wire n1_bit_adder_2_c_out, n1_bit_adder_3_c_out, n1_bit_adder_4_c_out, n1_bit_adder_5_c_out,
       n1_bit_adder_6_c_out, n1_bit_adder_7_c_out, n1_bit_adder_8_c_out, n1_bit_adder_9_c_out,
       n1_bit_adder_10_c_out, n1_bit_adder_11_c_out, n1_bit_adder_12_c_out, n1_bit_adder_13_c_out,
       n1_bit_adder_14_c_out, n1_bit_adder_15_c_out, n1_bit_adder_16_c_out, n1_bit_adder_17_c_out,
       n1_bit_adder_18_c_out, n1_bit_adder_19_c_out, n1_bit_adder_20_c_out, n1_bit_adder_21_c_out,
       n1_bit_adder_22_c_out, n1_bit_adder_23_c_out, n1_bit_adder_24_c_out, n1_bit_adder_25_c_out,
       n1_bit_adder_26_c_out, n1_bit_adder_27_c_out, n1_bit_adder_28_c_out, n1_bit_adder_29_c_out,
       n1_bit_adder_30_c_out, n1_bit_adder_31_c_out, n1_bit_adder_32_c_out, n1_bit_adder_33_c_out;

  _1_bit_Adder u_1_bit_adder_1 ();  // open: A, B, Arith__Op, Sum, C_Out, C_In
  _1_bit_Adder u_1_bit_adder_2 (
    .A(A[31]), .B(B[31]), .Arith__Op(Arith__Op), .Sum(Result[31]), .C_Out(n1_bit_adder_2_c_out),
    .C_In(n1_bit_adder_3_c_out));
  _1_bit_Adder u_1_bit_adder_3 (
    .A(A[30]), .B(B[30]), .Arith__Op(Arith__Op), .Sum(Result[30]), .C_Out(n1_bit_adder_3_c_out),
    .C_In(n1_bit_adder_4_c_out));
  _1_bit_Adder u_1_bit_adder_4 (
    .A(A[29]), .B(B[29]), .Arith__Op(Arith__Op), .Sum(Result[29]), .C_Out(n1_bit_adder_4_c_out),
    .C_In(n1_bit_adder_5_c_out));
  _1_bit_Adder u_1_bit_adder_5 (
    .A(A[28]), .B(B[28]), .Arith__Op(Arith__Op), .Sum(Result[28]), .C_Out(n1_bit_adder_5_c_out),
    .C_In(n1_bit_adder_6_c_out));
  _1_bit_Adder u_1_bit_adder_6 (
    .A(A[27]), .B(B[27]), .Arith__Op(Arith__Op), .Sum(Result[27]), .C_Out(n1_bit_adder_6_c_out),
    .C_In(n1_bit_adder_7_c_out));
  _1_bit_Adder u_1_bit_adder_7 (
    .A(A[26]), .B(B[26]), .Arith__Op(Arith__Op), .Sum(Result[26]), .C_Out(n1_bit_adder_7_c_out),
    .C_In(n1_bit_adder_8_c_out));
  _1_bit_Adder u_1_bit_adder_8 (
    .A(A[25]), .B(B[25]), .Arith__Op(Arith__Op), .Sum(Result[25]), .C_Out(n1_bit_adder_8_c_out),
    .C_In(n1_bit_adder_9_c_out));
  _1_bit_Adder u_1_bit_adder_9 (
    .A(A[24]), .B(B[24]), .Arith__Op(Arith__Op), .Sum(Result[24]), .C_Out(n1_bit_adder_9_c_out),
    .C_In(n1_bit_adder_10_c_out));
  _1_bit_Adder u_1_bit_adder_10 (
    .A(A[23]), .B(B[23]), .Arith__Op(Arith__Op), .Sum(Result[23]), .C_Out(n1_bit_adder_10_c_out),
    .C_In(n1_bit_adder_11_c_out));
  _1_bit_Adder u_1_bit_adder_11 (
    .A(A[22]), .B(B[22]), .Arith__Op(Arith__Op), .Sum(Result[22]), .C_Out(n1_bit_adder_11_c_out),
    .C_In(n1_bit_adder_12_c_out));
  _1_bit_Adder u_1_bit_adder_12 (
    .A(A[21]), .B(B[21]), .Arith__Op(Arith__Op), .Sum(Result[21]), .C_Out(n1_bit_adder_12_c_out),
    .C_In(n1_bit_adder_13_c_out));
  _1_bit_Adder u_1_bit_adder_13 (
    .A(A[20]), .B(B[20]), .Arith__Op(Arith__Op), .Sum(Result[20]), .C_Out(n1_bit_adder_13_c_out),
    .C_In(n1_bit_adder_14_c_out));
  _1_bit_Adder u_1_bit_adder_14 (
    .A(A[19]), .B(B[19]), .Arith__Op(Arith__Op), .Sum(Result[19]), .C_Out(n1_bit_adder_14_c_out),
    .C_In(n1_bit_adder_15_c_out));
  _1_bit_Adder u_1_bit_adder_15 (
    .A(A[18]), .B(B[18]), .Arith__Op(Arith__Op), .Sum(Result[18]), .C_Out(n1_bit_adder_15_c_out),
    .C_In(n1_bit_adder_16_c_out));
  _1_bit_Adder u_1_bit_adder_16 (
    .A(A[17]), .B(B[17]), .Arith__Op(Arith__Op), .Sum(Result[17]), .C_Out(n1_bit_adder_16_c_out),
    .C_In(n1_bit_adder_17_c_out));
  _1_bit_Adder u_1_bit_adder_17 (
    .A(A[16]), .B(B[16]), .Arith__Op(Arith__Op), .Sum(Result[16]), .C_Out(n1_bit_adder_17_c_out),
    .C_In(n1_bit_adder_18_c_out));
  _1_bit_Adder u_1_bit_adder_18 (
    .A(A[15]), .B(B[15]), .Arith__Op(Arith__Op), .Sum(Result[15]), .C_Out(n1_bit_adder_18_c_out),
    .C_In(n1_bit_adder_19_c_out));
  _1_bit_Adder u_1_bit_adder_19 (
    .A(A[14]), .B(B[14]), .Arith__Op(Arith__Op), .Sum(Result[14]), .C_Out(n1_bit_adder_19_c_out),
    .C_In(n1_bit_adder_20_c_out));
  _1_bit_Adder u_1_bit_adder_20 (
    .A(A[13]), .B(B[13]), .Arith__Op(Arith__Op), .Sum(Result[13]), .C_Out(n1_bit_adder_20_c_out),
    .C_In(n1_bit_adder_21_c_out));
  _1_bit_Adder u_1_bit_adder_21 (
    .A(A[12]), .B(B[12]), .Arith__Op(Arith__Op), .Sum(Result[12]), .C_Out(n1_bit_adder_21_c_out),
    .C_In(n1_bit_adder_22_c_out));
  _1_bit_Adder u_1_bit_adder_22 (
    .A(A[11]), .B(B[11]), .Arith__Op(Arith__Op), .Sum(Result[11]), .C_Out(n1_bit_adder_22_c_out),
    .C_In(n1_bit_adder_23_c_out));
  _1_bit_Adder u_1_bit_adder_23 (
    .A(A[10]), .B(B[10]), .Arith__Op(Arith__Op), .Sum(Result[10]), .C_Out(n1_bit_adder_23_c_out),
    .C_In(n1_bit_adder_24_c_out));
  _1_bit_Adder u_1_bit_adder_24 (
    .A(A[9]), .B(B[9]), .Arith__Op(Arith__Op), .Sum(Result[9]), .C_Out(n1_bit_adder_24_c_out),
    .C_In(n1_bit_adder_25_c_out));
  _1_bit_Adder u_1_bit_adder_25 (
    .A(A[8]), .B(B[8]), .Arith__Op(Arith__Op), .Sum(Result[8]), .C_Out(n1_bit_adder_25_c_out),
    .C_In(n1_bit_adder_26_c_out));
  _1_bit_Adder u_1_bit_adder_26 (
    .A(A[7]), .B(B[7]), .Arith__Op(Arith__Op), .Sum(Result[7]), .C_Out(n1_bit_adder_26_c_out),
    .C_In(n1_bit_adder_27_c_out));
  _1_bit_Adder u_1_bit_adder_27 (
    .A(A[6]), .B(B[6]), .Arith__Op(Arith__Op), .Sum(Result[6]), .C_Out(n1_bit_adder_27_c_out),
    .C_In(n1_bit_adder_28_c_out));
  _1_bit_Adder u_1_bit_adder_28 (
    .A(A[5]), .B(B[5]), .Arith__Op(Arith__Op), .Sum(Result[5]), .C_Out(n1_bit_adder_28_c_out),
    .C_In(n1_bit_adder_29_c_out));
  _1_bit_Adder u_1_bit_adder_29 (
    .A(A[4]), .B(B[4]), .Arith__Op(Arith__Op), .Sum(Result[4]), .C_Out(n1_bit_adder_29_c_out),
    .C_In(n1_bit_adder_30_c_out));
  _1_bit_Adder u_1_bit_adder_30 (
    .A(A[3]), .B(B[3]), .Arith__Op(Arith__Op), .Sum(Result[3]), .C_Out(n1_bit_adder_30_c_out),
    .C_In(n1_bit_adder_31_c_out));
  _1_bit_Adder u_1_bit_adder_31 (
    .A(A[2]), .B(B[2]), .Arith__Op(Arith__Op), .Sum(Result[2]), .C_Out(n1_bit_adder_31_c_out),
    .C_In(n1_bit_adder_32_c_out));
  _1_bit_Adder u_1_bit_adder_32 (
    .A(A[1]), .B(B[1]), .Arith__Op(Arith__Op), .Sum(Result[1]), .C_Out(n1_bit_adder_32_c_out),
    .C_In(n1_bit_adder_33_c_out));
  _1_bit_Adder u_1_bit_adder_33 (
    .A(A[0]), .B(B[0]), .Arith__Op(Arith__Op), .Sum(Result[0]), .C_Out(n1_bit_adder_33_c_out),
    .C_In(Arith__Op));
  xor xor_1 (Overflow, n1_bit_adder_3_c_out, n1_bit_adder_2_c_out);
endmodule

module ALU_MAIN (
  input  [3:0] ALU_Op,
  input  [31:0] A,
  input  [31:0] B,
  output [31:0] out_4,
  output Overflow,
  output Zero
);

  wire and_2_out, or_1_out;
  wire [1:0] or_2_out, undriven;
  wire [4:0] undriven_2;
  wire [31:0] and_3_out, multiplexer_1_out, n32_bit_adder_1_result, or_3_out, shifter_1_shift_result,
       sign_slt_result_1_out_3, xor_1_out;

  or or_1 (or_1_out, ALU_Op[0], and_2_out);
  or or_2 (or_2_out[0], ALU_Op[2], ALU_Op[3]);
  and and_1 (or_2_out[1], ~ALU_Op[0], ALU_Op[1], ALU_Op[2]);  // AND_Gate
  and and_2 (and_2_out, or_2_out[0], or_2_out[1]);
  assign and_3_out = A & B;  // AND_Gate and_3, 32 bits wide
  assign or_3_out = A | B;  // OR_Gate or_3, 32 bits wide
  assign xor_1_out = A ^ B;  // XOR_Gate xor_1, 32 bits wide
  Shifter shifter_1 (
    .Shift_Rotate_Op(undriven), .Shift_Amount(undriven_2), .B(B), .Shift_Result(shifter_1_shift_result));
  _32_bit_Adder u_32_bit_adder_1 (
    .Result(n32_bit_adder_1_result), .A(A), .B(B), .Arith__Op(or_1_out), .Overflow(Overflow));
  Sign___SLT_Result sign_slt_result_1 (
    .in_1(n32_bit_adder_1_result), .Overflow(Overflow), .out_3(sign_slt_result_1_out_3));
  Multiplexer #(.select(2), .width(32)) multiplexer_1 (
    .in1(and_3_out), .in2(or_3_out), .in3(xor_1_out), .out(multiplexer_1_out), .sel(ALU_Op[1:0]));  // open: in0, en
  Multiplexer #(.select(2), .width(32)) multiplexer_2 (
    .in0(multiplexer_1_out), .in1(n32_bit_adder_1_result), .in3(sign_slt_result_1_out_3), .out(out_4),
    .sel(or_2_out));  // open: in2, en
  _32_bit_NOR u_32_bit_nor_1 (.INput(out_4), .Zero(Zero));

  // Notes on the sheet:
  //   "Decode ALU OP section"
  //   Shift/Rotate Op
  //   Shift Amount
  //   is_arith
  //   is_slt
  //   Arith Op
  //   Logic Op
  //   SLT
  //   Arith
  //   Logic
  //   ALU Select
  //   NECESSARY INSTRUCTIONS:
  //   Add, Sub, And, Or, Xor, SLT
endmodule

module Sign___SLT_Result (
  input  [31:0] in_1,
  input  Overflow,
  output [31:0] out_3
);

  wire xor_1_out;

  xor xor_1 (xor_1_out, in_1[31], Overflow);
  and and_1 (out_3[0], xor_1_out, ~Overflow);  // AND_Gate

  assign out_3[31:1] = {31{1'b0}};
endmodule

module _32_bit_NOR (
  input  [31:0] INput,
  output Zero
);

  nor nor_1 (Zero, INput[0], INput[1], INput[2], INput[3], INput[4], INput[5], INput[6], INput[7], INput[8], INput[9], INput[10], INput[11], INput[12], INput[13], INput[14], INput[15], INput[16], INput[17], INput[18], INput[19], INput[20], INput[21], INput[22], INput[23], INput[24], INput[25], INput[26], INput[27], INput[28], INput[29], INput[30], INput[31]);
endmodule
