// Logisim project ALU_OP Analyzer.circ as structural Verilog: 1 circuit, main circuit main
module main (
  input  [3:0] in_1,
  output Arith__Op,
  output [1:0] Logic_Op,
  output [1:0] ALU_Sel
);

  or or_1 (ALU_Sel[0], in_1[2], in_1[3]);
  and and_1 (ALU_Sel[1], ~in_1[0], in_1[1], in_1[2]);  // AND_Gate

  assign Arith__Op = in_1[0];
  assign Logic_Op = in_1[1:0];

  // Notes on the sheet:
  //   0001 logic and
  //   0010 logic or
  //   0011 logix xor
  //   0100 arith add
  //   0101 arith sub
  //   0110 slt
  //   this is ugly as balls but it works
  //   input
  //   is_arith
  //   is_slt
  //   ALU INPUTS MUST MATCH THESE
  //   NICK DOUBLE CHECK THIS 
  //   0 = Add
  //   1 = Sub
  //   01 and
  //   10 or
  //   11 xor
  //   00 logic
  //   01 arith
  //   11 slt
  //   4 bit input:
  //   01XX = Arith
  //   0110 SLT
  //   00XX = Logic
  //   XX01 = And
  //   XX10 = Or
  //   XX11 = Xor
  //   XX00 = Add
  //   XX01 = Sub
endmodule
