// Logisim project Branch_module.circ as structural Verilog: 1 circuit, main circuit main
module main (
  input  Zero,
  input  Beq,
  input  Bne,
  output Branch
);

  wire and_1_out, and_2_out;

  and and_1 (and_1_out, Zero, Beq);
  and and_2 (and_2_out, ~Zero, Bne);  // AND_Gate
  or or_1 (Branch, and_1_out, and_2_out);
endmodule
