// Logisim project Control_Unit.circ as structural Verilog: 1 circuit, main circuit main
module main (
  input  [5:0] Opcode,
  output RegDst,
  output RegWrite,
  output ExtOp,
  output ALUSrc,
  output Beq,
  output Jump,
  output MemRead,
  output MemWrite,
  output MemToReg,
  output [2:0] ALUOp,
  output BNE
);

  wire and_3_out, and_4_out, and_5_out, and_9_out, and_10_out, and_11_out, and_12_out, and_13_out,
       and_14_out, not_1_out, not_2_out, not_3_out, not_4_out, not_5_out, not_6_out, not_7_out, not_8_out,
       not_9_out, not_10_out, not_12_out, not_13_out, not_14_out, not_15_out, not_16_out, not_17_out,
       not_18_out, not_19_out, not_20_out, not_21_out, not_22_out;

  not not_1 (not_1_out, Opcode[5]);
  not not_2 (not_2_out, Opcode[4]);
  not not_3 (not_3_out, Opcode[3]);
  not not_4 (not_4_out, Opcode[1]);
  not not_5 (not_5_out, Opcode[3]);
  not not_6 (not_6_out, Opcode[0]);
  not not_7 (not_7_out, Opcode[2]);
  not not_8 (not_8_out, Opcode[1]);
  not not_9 (not_9_out, Opcode[5]);
  not not_10 (not_10_out, Opcode[3]);
  not not_11 (ExtOp, Opcode[2]);
  or or_1 (ALUSrc, Opcode[1], Opcode[3]);
  not not_12 (not_12_out, Opcode[3]);
  not not_13 (not_13_out, Opcode[0]);
  not not_14 (not_14_out, Opcode[3]);
  not not_15 (not_15_out, Opcode[0]);
  not not_16 (not_16_out, Opcode[3]);
  and and_1 (MemWrite, Opcode[5], Opcode[3]);
  not not_17 (not_17_out, Opcode[3]);
  not not_18 (not_18_out, Opcode[2]);
  not not_19 (not_19_out, Opcode[0]);
  not not_20 (not_20_out, Opcode[1]);
  not not_21 (not_21_out, Opcode[3]);
  not not_22 (not_22_out, Opcode[0]);
  and and_2 (RegDst, not_5_out, not_6_out);
  and and_3 (and_3_out, not_7_out, not_8_out);
  or or_2 (RegWrite, and_3_out, and_4_out, and_5_out);
  and and_4 (and_4_out, not_9_out, Opcode[3]);
  and and_5 (and_5_out, Opcode[5], not_10_out);
  and and_6 (Beq, not_12_out, Opcode[2], not_13_out);
  and and_7 (Jump, not_14_out, Opcode[1], not_15_out);
  and and_8 (MemRead, Opcode[5], not_16_out);
  and and_9 (and_9_out, not_17_out, Opcode[2]);
  or or_3 (ALUOp[2], and_9_out, and_10_out, Opcode[5]);
  and and_10 (and_10_out, Opcode[3], not_18_out);
  and and_11 (and_11_out, Opcode[1], not_19_out);
  or or_4 (ALUOp[1], and_11_out, and_12_out);
  and and_12 (and_12_out, Opcode[3], not_20_out, Opcode[0]);
  and and_13 (and_13_out, not_21_out, Opcode[2]);
  or or_5 (ALUOp[0], and_13_out, and_14_out);
  and and_14 (and_14_out, Opcode[2], not_22_out);
  and and_15 (BNE, not_1_out, not_2_out, not_3_out, Opcode[2], not_4_out, Opcode[0]);

  assign MemToReg = Opcode[5];
endmodule
