// Logisim project Extender.circ as structural Verilog: 1 circuit, main circuit main
module main (
  input  [15:0] Immd16,
  input  ExtOp,
  output [31:0] Output
);

  and and_1 (Output[31], Immd16[15], ExtOp);

  assign Output[30:0] = {{15{Output[31]}}, Immd16};
endmodule
