// Logisim project Processor_Finished.circ as structural Verilog: 2 circuits, main circuit main
module main (
);

  wire ALUSrc, Beq, Bne, button_1_out, clk, ExtOp, Jump, main_6_branch, MemRead, MemtoReg, MemWrite, RegDst,
       RegWrite, Zero;
  wire [2:0] ALUOp;
  wire [3:0] main_5_out_3, plus_1_out_2;
  wire [4:0] multiplexer_1_out;
  wire [5:0] Op;
  wire [25:0] main_1_data;
  wire [27:0] plus_1_out_2_2;
  wire [31:0] adder_1_out, alu_main_1_out_4, main_3_output, main_4_busa, main_4_busb, main_7_data_out,
       multiplexer_2_out, multiplexer_3_out, multiplexer_4_out, multiplexer_5_out, PC_q, shifter_1_out;

  // Probe on PC_q
  Register #(.width(32)) PC (.D(multiplexer_4_out), .Q(PC_q), .clk(clk), .clr(button_1_out));  // open: en
  Button button_1 (.out(button_1_out));
  Clock clock_1 (.out(clk));
  PC_Adder plus_1 (.PC(PC_q), .out_2({plus_1_out_2, plus_1_out_2_2}));
  _2_32_memory_ROM_main main_1 (.Address(PC_q), .Data({Op, main_1_data}));
  // Probe on {Op, main_1_data}
  Control_Unit_main main_2 (
    .Opcode(Op), .RegDst(RegDst), .RegWrite(RegWrite), .ExtOp(ExtOp), .ALUSrc(ALUSrc), .Beq(Beq),
    .Jump(Jump), .MemRead(MemRead), .MemWrite(MemWrite), .MemToReg(MemtoReg), .ALUOp(ALUOp), .BNE(Bne));
  // Probe on main_1_data[25:21]
  // Probe on main_1_data[20:16]
  Multiplexer #(.width(5), .enable("false")) multiplexer_1 (
    .in0(main_1_data[20:16]), .in1(main_1_data[15:11]), .out(multiplexer_1_out), .sel(RegDst));
  Extender_main main_3 (.Immd16(main_1_data[15:0]), .ExtOp(ExtOp), .Output(main_3_output));
  Register_file_main main_4 (
    .RA(main_1_data[25:21]), .RB(main_1_data[20:16]), .RW(multiplexer_1_out), .BusW(multiplexer_5_out),
    .BusB(main_4_busb), .BusA(main_4_busa), .RegWrite(RegWrite), .Clk(clk));
  // Probe on multiplexer_5_out
  // Probe on main_3_output
  // Probe on main_4_busa
  ALUCTrl_main main_5 (.func(main_1_data[5:0]), .ALUOp(ALUOp), .out_3(main_5_out_3));
  Shifter #(.width(32)) shifter_1 (.in(main_3_output), .\dist (5'b00010), .out(shifter_1_out));
  // Probe on main_4_busb
  Multiplexer #(.width(32), .enable("false")) multiplexer_2 (
    .in0(main_4_busb), .in1(main_3_output), .out(multiplexer_2_out), .sel(ALUSrc));
  // Probe on multiplexer_2_out
  Adder #(.width(32)) adder_1 (
    .a({plus_1_out_2, plus_1_out_2_2}), .b(shifter_1_out), .out(adder_1_out));  // open: cin, cout
  Multiplexer #(.width(32), .enable("false")) multiplexer_3 (
    .in0({plus_1_out_2, plus_1_out_2_2}), .in1(adder_1_out), .out(multiplexer_3_out), .sel(main_6_branch));
  Branch_module_main main_6 (.Zero(Zero), .Beq(Beq), .Bne(Bne), .Branch(main_6_branch));
  ALU_MAIN alu_main_1 (
    .out_4(alu_main_1_out_4), .Zero(Zero), .A(main_4_busa), .B(multiplexer_2_out), .ALU_Op(main_5_out_3));  // open: Overflow
  Multiplexer #(.width(32), .enable("false")) multiplexer_4 (
    .in0(multiplexer_3_out), .in1({plus_1_out_2, main_1_data, 2'b00}), .out(multiplexer_4_out), .sel(Jump));
  // Probe on alu_main_1_out_4
  // Probe on main_4_busb
  // Probe on main_7_data_out
  _2_32_memory_with_Control_main main_7 (
    .Address(alu_main_1_out_4), .MemWrite(MemWrite), .MemRead(MemRead), .Data_In(main_4_busb),
    .Data_Out(main_7_data_out), .Clk(clk));
  Multiplexer #(.width(32), .enable("false")) multiplexer_5 (
    .in0(alu_main_1_out_4), .in1(main_7_data_out), .out(multiplexer_5_out), .sel(MemtoReg));

  // Notes on the sheet:
  //   Extender
  //   ALU Ctrl
endmodule

module PC_Adder (
  input  [31:0] PC,
  output [31:0] out_2
);

  Adder #(.width(32)) adder_1 (.a(PC), .b(32'h1), .out(out_2));  // open: cin, cout
endmodule
