// Logisim project Register file.circ as structural Verilog: 1 circuit, main circuit main
module main (
  input  [4:0] RA,
  input  [4:0] RB,
  input  [4:0] RW,
  input  [31:0] BusW,
  input  Clk,
  input  RegWrite,
  output [31:0] BusB,
  output [31:0] BusA
);

  wire and_1_out, and_2_out, and_3_out, and_4_out, and_5_out, and_6_out, and_7_out, and_8_out, and_9_out,
       and_10_out, and_11_out, and_12_out, and_13_out, and_14_out, and_15_out, and_16_out, and_17_out,
       and_18_out, and_19_out, and_20_out, and_21_out, and_22_out, and_23_out, and_24_out, and_25_out,
       and_26_out, and_27_out, and_28_out, and_29_out, and_30_out, and_31_out, decoder_2_out0,
       decoder_3_out0, n1, n2, n3, n4, n5, n6, n7, n8, n9, n10, n11, n12, n13, n14, n15, n16, n17, n18, n19,
       n20, n21, n22, n23, n24, n25, n26, n27, n28, n29, n30, n31, R0, R1, R2, R3, R4, R5, R6, R7, R8, R9,
       R10, R11, R12, R13, R14, R15, R16, R17, R18, R19, R20, R21, R22, R23, R24, R25, R26, R27, R28, R29,
       R30, R31, s0, S1, S2, S3, S4, S5, S6, S7, S8, S9, S10, S11, S12, S13, S14, S15, S16, S17, S18, S19,
       S20, S21, S22, S23, S24, S25, S26, S27, S28, S29, S30, S31;
  wire [31:0] A0, b0, register_1_q, register_2_q, register_3_q, register_4_q, register_5_q, register_6_q,
       register_7_q, register_8_q, register_9_q, register_10_q, register_11_q, register_12_q, register_13_q,
       register_14_q, register_15_q, register_16_q, register_17_q, register_18_q, register_19_q,
       register_20_q, register_21_q, register_22_q, register_23_q, register_24_q, register_25_q,
       register_26_q, register_27_q, register_28_q, register_29_q, register_30_q, register_31_q,
       register_32_q;

  Decoder #(.select(5)) decoder_1 (
    .out1(n1), .out2(n2), .out3(n3), .out4(n4), .out5(n5), .out6(n6), .out7(n7), .out8(n8), .out9(n9),
    .out10(n10), .out11(n11), .out12(n12), .out13(n13), .out14(n14), .out15(n15), .out16(n16), .out17(n17),
    .out18(n18), .out19(n19), .out20(n20), .out21(n21), .out22(n22), .out23(n23), .out24(n24), .out25(n25),
    .out26(n26), .out27(n27), .out28(n28), .out29(n29), .out30(n30), .out31(n31), .sel(RW));  // open: out0, en
  Register #(.width(32)) register_1 (.Q(register_1_q), .clk(Clk));  // open: D, en, clr
  Register #(.width(32)) register_2 (.D(BusW), .en(and_1_out), .Q(register_2_q), .clk(Clk));  // open: clr
  and and_1 (and_1_out, n4, RegWrite);
  Register #(.width(32)) register_3 (.D(BusW), .en(and_2_out), .Q(register_3_q), .clk(Clk));  // open: clr
  and and_2 (and_2_out, n8, RegWrite);
  Register #(.width(32)) register_4 (.D(BusW), .en(and_3_out), .Q(register_4_q), .clk(Clk));  // open: clr
  and and_3 (and_3_out, n12, RegWrite);
  Register #(.width(32)) register_5 (.D(BusW), .en(and_4_out), .Q(register_5_q), .clk(Clk));  // open: clr
  and and_4 (and_4_out, n16, RegWrite);
  Register #(.width(32)) register_6 (.D(BusW), .en(and_5_out), .Q(register_6_q), .clk(Clk));  // open: clr
  and and_5 (and_5_out, n20, RegWrite);
  Register #(.width(32)) register_7 (.D(BusW), .en(and_6_out), .Q(register_7_q), .clk(Clk));  // open: clr
  and and_6 (and_6_out, n24, RegWrite);
  Register #(.width(32)) register_8 (.D(BusW), .en(and_7_out), .Q(register_8_q), .clk(Clk));  // open: clr
  and and_7 (and_7_out, n28, RegWrite);
  assign b0 = s0 ? register_1_q : 32'bz;  // Controlled_Buffer controlled_buffer_1
  assign A0 = R0 ? register_1_q : 32'bz;  // Controlled_Buffer controlled_buffer_2
  assign BusB = S4 ? register_2_q : 32'bz;  // Controlled_Buffer controlled_buffer_3
  assign BusA = R4 ? register_2_q : 32'bz;  // Controlled_Buffer controlled_buffer_4
  assign BusB = S8 ? register_3_q : 32'bz;  // Controlled_Buffer controlled_buffer_5
  assign BusA = R8 ? register_3_q : 32'bz;  // Controlled_Buffer controlled_buffer_6
  assign BusB = S12 ? register_4_q : 32'bz;  // Controlled_Buffer controlled_buffer_7
  assign BusA = R12 ? register_4_q : 32'bz;  // Controlled_Buffer controlled_buffer_8
  assign BusB = S16 ? register_5_q : 32'bz;  // Controlled_Buffer controlled_buffer_9
  assign BusA = R16 ? register_5_q : 32'bz;  // Controlled_Buffer controlled_buffer_10
  assign BusB = S20 ? register_6_q : 32'bz;  // Controlled_Buffer controlled_buffer_11
  assign BusA = R20 ? register_6_q : 32'bz;  // Controlled_Buffer controlled_buffer_12
  assign BusB = S24 ? register_7_q : 32'bz;  // Controlled_Buffer controlled_buffer_13
  assign BusA = R24 ? register_7_q : 32'bz;  // Controlled_Buffer controlled_buffer_14
  assign BusB = S28 ? register_8_q : 32'bz;  // Controlled_Buffer controlled_buffer_15
  assign BusA = R28 ? register_8_q : 32'bz;  // Controlled_Buffer controlled_buffer_16
  Register #(.width(32)) register_9 (.D(BusW), .en(and_8_out), .Q(register_9_q), .clk(Clk));  // open: clr
  and and_8 (and_8_out, n1, RegWrite);
  Register #(.width(32)) register_10 (.D(BusW), .en(and_9_out), .Q(register_10_q), .clk(Clk));  // open: clr
  and and_9 (and_9_out, n5, RegWrite);
  Register #(.width(32)) register_11 (.D(BusW), .en(and_10_out), .Q(register_11_q), .clk(Clk));  // open: clr
  and and_10 (and_10_out, n9, RegWrite);
  Register #(.width(32)) register_12 (.D(BusW), .en(and_11_out), .Q(register_12_q), .clk(Clk));  // open: clr
  and and_11 (and_11_out, n13, RegWrite);
  Register #(.width(32)) register_13 (.D(BusW), .en(and_12_out), .Q(register_13_q), .clk(Clk));  // open: clr
  and and_12 (and_12_out, n17, RegWrite);
  Register #(.width(32)) register_14 (.D(BusW), .en(and_13_out), .Q(register_14_q), .clk(Clk));  // open: clr
  and and_13 (and_13_out, n21, RegWrite);
  Register #(.width(32)) register_15 (.D(BusW), .en(and_14_out), .Q(register_15_q), .clk(Clk));  // open: clr
  and and_14 (and_14_out, n25, RegWrite);
  Register #(.width(32)) register_16 (.D(BusW), .en(and_15_out), .Q(register_16_q), .clk(Clk));  // open: clr
  and and_15 (and_15_out, n29, RegWrite);
  assign BusB = S1 ? register_9_q : 32'bz;  // Controlled_Buffer controlled_buffer_17
  assign BusA = R1 ? register_9_q : 32'bz;  // Controlled_Buffer controlled_buffer_18
  assign BusB = S5 ? register_10_q : 32'bz;  // Controlled_Buffer controlled_buffer_19
  assign BusA = R5 ? register_10_q : 32'bz;  // Controlled_Buffer controlled_buffer_20
  assign BusB = S9 ? register_11_q : 32'bz;  // Controlled_Buffer controlled_buffer_21
  assign BusA = R9 ? register_11_q : 32'bz;  // Controlled_Buffer controlled_buffer_22
  assign BusB = S13 ? register_12_q : 32'bz;  // Controlled_Buffer controlled_buffer_23
  assign BusA = R13 ? register_12_q : 32'bz;  // Controlled_Buffer controlled_buffer_24
  assign BusB = S17 ? register_13_q : 32'bz;  // Controlled_Buffer controlled_buffer_25
  assign BusA = R17 ? register_13_q : 32'bz;  // Controlled_Buffer controlled_buffer_26
  assign BusB = S21 ? register_14_q : 32'bz;  // Controlled_Buffer controlled_buffer_27
  assign BusA = R21 ? register_14_q : 32'bz;  // Controlled_Buffer controlled_buffer_28
  assign BusB = S25 ? register_15_q : 32'bz;  // Controlled_Buffer controlled_buffer_29
  assign BusA = R25 ? register_15_q : 32'bz;  // Controlled_Buffer controlled_buffer_30
  assign BusB = S29 ? register_16_q : 32'bz;  // Controlled_Buffer controlled_buffer_31
  assign BusA = R29 ? register_16_q : 32'bz;  // Controlled_Buffer controlled_buffer_32
  Register #(.width(32)) register_17 (.D(BusW), .en(and_16_out), .Q(register_17_q), .clk(Clk));  // open: clr
  and and_16 (and_16_out, n2, RegWrite);
  Register #(.width(32)) register_18 (.D(BusW), .en(and_17_out), .Q(register_18_q), .clk(Clk));  // open: clr
  and and_17 (and_17_out, n6, RegWrite);
  Register #(.width(32)) register_19 (.D(BusW), .en(and_18_out), .Q(register_19_q), .clk(Clk));  // open: clr
  and and_18 (and_18_out, n10, RegWrite);
  Register #(.width(32)) register_20 (.D(BusW), .en(and_19_out), .Q(register_20_q), .clk(Clk));  // open: clr
  and and_19 (and_19_out, n14, RegWrite);
  Register #(.width(32)) register_21 (.D(BusW), .en(and_20_out), .Q(register_21_q), .clk(Clk));  // open: clr
  and and_20 (and_20_out, n18, RegWrite);
  Register #(.width(32)) register_22 (.D(BusW), .en(and_21_out), .Q(register_22_q), .clk(Clk));  // open: clr
  and and_21 (and_21_out, n22, RegWrite);
  Register #(.width(32)) register_23 (.D(BusW), .en(and_22_out), .Q(register_23_q), .clk(Clk));  // open: clr
  and and_22 (and_22_out, n26, RegWrite);
  Register #(.width(32)) register_24 (.D(BusW), .en(and_23_out), .Q(register_24_q), .clk(Clk));  // open: clr
  and and_23 (and_23_out, n30, RegWrite);
  assign BusB = S2 ? register_17_q : 32'bz;  // Controlled_Buffer controlled_buffer_33
  assign BusA = R2 ? register_17_q : 32'bz;  // Controlled_Buffer controlled_buffer_34
  assign BusB = S6 ? register_18_q : 32'bz;  // Controlled_Buffer controlled_buffer_35
  assign BusA = R6 ? register_18_q : 32'bz;  // Controlled_Buffer controlled_buffer_36
  assign BusB = S10 ? register_19_q : 32'bz;  // Controlled_Buffer controlled_buffer_37
  assign BusA = R10 ? register_19_q : 32'bz;  // Controlled_Buffer controlled_buffer_38
  assign BusB = S14 ? register_20_q : 32'bz;  // Controlled_Buffer controlled_buffer_39
  assign BusA = R14 ? register_20_q : 32'bz;  // Controlled_Buffer controlled_buffer_40
  assign BusB = S18 ? register_21_q : 32'bz;  // Controlled_Buffer controlled_buffer_41
  assign BusA = R18 ? register_21_q : 32'bz;  // Controlled_Buffer controlled_buffer_42
  assign BusB = S22 ? register_22_q : 32'bz;  // Controlled_Buffer controlled_buffer_43
  assign BusA = R22 ? register_22_q : 32'bz;  // Controlled_Buffer controlled_buffer_44
  assign BusB = S26 ? register_23_q : 32'bz;  // Controlled_Buffer controlled_buffer_45
  assign BusA = R26 ? register_23_q : 32'bz;  // Controlled_Buffer controlled_buffer_46
  assign BusB = S30 ? register_24_q : 32'bz;  // Controlled_Buffer controlled_buffer_47
  assign BusA = R30 ? register_24_q : 32'bz;  // Controlled_Buffer controlled_buffer_48
  and and_24 (and_24_out, n3, RegWrite);
  and and_25 (and_25_out, n7, RegWrite);
  and and_26 (and_26_out, n11, RegWrite);
  and and_27 (and_27_out, n15, RegWrite);
  and and_28 (and_28_out, n19, RegWrite);
  and and_29 (and_29_out, n23, RegWrite);
  and and_30 (and_30_out, n27, RegWrite);
  and and_31 (and_31_out, n31, RegWrite);
  assign BusB = S3 ? register_25_q : 32'bz;  // Controlled_Buffer controlled_buffer_49
  Register #(.width(32)) register_25 (.D(BusW), .en(and_24_out), .Q(register_25_q), .clk(Clk));  // open: clr
  assign BusA = R3 ? register_25_q : 32'bz;  // Controlled_Buffer controlled_buffer_50
  assign BusB = S7 ? register_26_q : 32'bz;  // Controlled_Buffer controlled_buffer_51
  assign BusA = R7 ? register_26_q : 32'bz;  // Controlled_Buffer controlled_buffer_52
  Register #(.width(32)) register_26 (.D(BusW), .en(and_25_out), .Q(register_26_q), .clk(Clk));  // open: clr
  assign BusB = S11 ? register_27_q : 32'bz;  // Controlled_Buffer controlled_buffer_53
  assign BusA = R11 ? register_27_q : 32'bz;  // Controlled_Buffer controlled_buffer_54
  Register #(.width(32)) register_27 (.D(BusW), .en(and_26_out), .Q(register_27_q), .clk(Clk));  // open: clr
  assign BusB = S15 ? register_28_q : 32'bz;  // Controlled_Buffer controlled_buffer_55
  Register #(.width(32)) register_28 (.D(BusW), .en(and_27_out), .Q(register_28_q), .clk(Clk));  // open: clr
  assign BusA = R15 ? register_28_q : 32'bz;  // Controlled_Buffer controlled_buffer_56
  assign BusB = S19 ? register_29_q : 32'bz;  // Controlled_Buffer controlled_buffer_57
  assign BusA = R19 ? register_29_q : 32'bz;  // Controlled_Buffer controlled_buffer_58
  Register #(.width(32)) register_29 (.D(BusW), .en(and_28_out), .Q(register_29_q), .clk(Clk));  // open: clr
  assign BusB = S23 ? register_30_q : 32'bz;  // Controlled_Buffer controlled_buffer_59
  Register #(.width(32)) register_30 (.D(BusW), .en(and_29_out), .Q(register_30_q), .clk(Clk));  // open: clr
  assign BusA = R23 ? register_30_q : 32'bz;  // Controlled_Buffer controlled_buffer_60
  assign BusB = S27 ? register_31_q : 32'bz;  // Controlled_Buffer controlled_buffer_61
  Register #(.width(32)) register_31 (.D(BusW), .en(and_30_out), .Q(register_31_q), .clk(Clk));  // open: clr
  assign BusA = R27 ? register_31_q : 32'bz;  // Controlled_Buffer controlled_buffer_62
  assign BusB = S31 ? register_32_q : 32'bz;  // Controlled_Buffer controlled_buffer_63
  assign BusA = R31 ? register_32_q : 32'bz;  // Controlled_Buffer controlled_buffer_64
  Register #(.width(32)) register_32 (.D(BusW), .en(and_31_out), .Q(register_32_q), .clk(Clk));  // open: clr
  Decoder #(.select(5)) decoder_2 (
    .out0(decoder_2_out0), .out1(R1), .out2(R2), .out3(R3), .out4(R4), .out5(R5), .out6(R6), .out7(R7),
    .out8(R8), .out9(R9), .out10(R10), .out11(R11), .out12(R12), .out13(R13), .out14(R14), .out15(R15),
    .out16(R16), .out17(R17), .out18(R18), .out19(R19), .out20(R20), .out21(R21), .out22(R22), .out23(R23),
    .out24(R24), .out25(R25), .out26(R26), .out27(R27), .out28(R28), .out29(R29), .out30(R30), .out31(R31),
    .sel(RA));  // open: en
  assign BusA = decoder_2_out0 ? {32{1'b0}} : 32'bz;  // Controlled_Buffer controlled_buffer_65
  Decoder #(.select(5)) decoder_3 (
    .out0(decoder_3_out0), .out1(S1), .out2(S2), .out3(S3), .out4(S4), .out5(S5), .out6(S6), .out7(S7),
    .out8(S8), .out9(S9), .out10(S10), .out11(S11), .out12(S12), .out13(S13), .out14(S14), .out15(S15),
    .out16(S16), .out17(S17), .out18(S18), .out19(S19), .out20(S20), .out21(S21), .out22(S22), .out23(S23),
    .out24(S24), .out25(S25), .out26(S26), .out27(S27), .out28(S28), .out29(S29), .out30(S30), .out31(S31),
    .sel(RB));  // open: en
  assign BusB = decoder_3_out0 ? {32{1'b0}} : 32'bz;  // Controlled_Buffer controlled_buffer_66

  // Other names for the same wires on the sheet: A1[31:0] = BusA; A2[31:0] = BusA; A3[31:0] = BusA; A4[31:0] = BusA;
  //   A5[31:0] = BusA; A6[31:0] = BusA; A7[31:0] = BusA; A8[31:0] = BusA; A9[31:0] = BusA; A10[31:0] = BusA;
  //   A11[31:0] = BusA; A12[31:0] = BusA; A13[31:0] = BusA; A14[31:0] = BusA; A15[31:0] = BusA; A16[31:0] = BusA;
  //   A17[31:0] = BusA; A18[31:0] = BusA; A19[31:0] = BusA; A20[31:0] = BusA; A21[31:0] = BusA; A22[31:0] = BusA;
  //   A23[31:0] = BusA; A24[31:0] = BusA; A25[31:0] = BusA; A26[31:0] = BusA; A27[31:0] = BusA; A28[31:0] = BusA;
  //   A29[31:0] = BusA; A30[31:0] = BusA; A31[31:0] = BusA; B1[31:0] = BusB; B2[31:0] = BusB; B3[31:0] = BusB;
  //   B4[31:0] = BusB; B5[31:0] = BusB; B6[31:0] = BusB; B7[31:0] = BusB; B8[31:0] = BusB; B9[31:0] = BusB;
  //   B10[31:0] = BusB; B11[31:0] = BusB; B12[31:0] = BusB; B13[31:0] = BusB; B14[31:0] = BusB; B15[31:0] = BusB;
  //   B16[31:0] = BusB; B17[31:0] = BusB; B18[31:0] = BusB; B19[31:0] = BusB; B20[31:0] = BusB; B21[31:0] = BusB;
  //   B22[31:0] = BusB; B23[31:0] = BusB; B24[31:0] = BusB; B25[31:0] = BusB; B26[31:0] = BusB; B27[31:0] = BusB;
  //   B28[31:0] = BusB; B29[31:0] = BusB; B30[31:0] = BusB; B31[31:0] = BusB
endmodule
